// Logisim project OneBit.circ as structural Verilog: 11 circuits, main circuit main
module main (
  input  _2,
  input  _1,
  input  _0,
  input  Data,
  input  Reset,
  input  Clock
);

  wire A_2_data, A_2_write_data, alu2_1_p, alu2_1_s, alu2_1_write_data, B, B_2_data, B_2_write_data, C_data,
       C_write_data, Cell_0_data, Cell_0_write_data, Cell_1_data, Cell_1_write_data,
       decoderopt_1_a_read_enable, decoderopt_1_ab_write_enable, decoderopt_1_alu_s_p,
       decoderopt_1_alu_write_enable, decoderopt_1_b_read_enable, decoderopt_1_bus_data,
       decoderopt_1_c_read_enable, decoderopt_1_c_write_enable, decoderopt_1_ram_address,
       decoderopt_1_ram_read_enable, decoderopt_1_ram_write_enable, ram_1_re_0, ram_1_re_1, ram_1_we_0,
       ram_1_we_1;

  DecoderOpt decoderopt_1 (
    .Data(Data), ._2(_2), ._1(_1), ._0(_0), .A_Read_Enable(decoderopt_1_a_read_enable),
    .B_Read_Enable(decoderopt_1_b_read_enable), .AB_Write_Enable(decoderopt_1_ab_write_enable),
    .C_Read_Enable(decoderopt_1_c_read_enable), .C_Write_Enable(decoderopt_1_c_write_enable),
    .Alu_Write_Enable(decoderopt_1_alu_write_enable), .Alu_S_P(decoderopt_1_alu_s_p),
    .Ram_Read_Enable(decoderopt_1_ram_read_enable), .Ram_Write_Enable(decoderopt_1_ram_write_enable),
    .Ram_Address(decoderopt_1_ram_address), .Bus_Data(decoderopt_1_bus_data));
  Ram ram_1 (
    .Read_Enable(decoderopt_1_ram_read_enable), .Write_Enable(decoderopt_1_ram_write_enable),
    .Address(decoderopt_1_ram_address), .RE_0(ram_1_re_0), .WE_0(ram_1_we_0), .RE_1(ram_1_re_1),
    .WE_1(ram_1_we_1));
  Register Cell_0 (
    .Clock(Clock), .Read_Enable(ram_1_re_0), .Read_Data(B), .Write_Enable(ram_1_we_0),
    .Write_Data(Cell_0_write_data), .Reset(Reset), .Data(Cell_0_data));
  Register Cell_1 (
    .Clock(Clock), .Read_Enable(ram_1_re_1), .Read_Data(B), .Write_Enable(ram_1_we_1),
    .Write_Data(Cell_1_write_data), .Reset(Reset), .Data(Cell_1_data));
  Bus bus_1 (
    .Bus_Input(Cell_1_write_data), .Bus_Input_2(Cell_0_write_data), .Bus_Input_3(decoderopt_1_bus_data),
    .Bus_Input_4(alu2_1_write_data), .Bus_Input_5(C_write_data), .Bus_Output(B));
  ALU2 alu2_1 (
    .A(A_2_write_data), .B(B_2_write_data), .Write_Enable(decoderopt_1_alu_write_enable),
    .Write_Data(alu2_1_write_data), .S_P(decoderopt_1_alu_s_p), .S(alu2_1_s), .P(alu2_1_p));
  // Probe on ram_1_re_0
  // Probe on B
  // Probe on ram_1_we_0
  // Probe on Cell_0_write_data
  // Probe on Cell_0_data
  // Probe on ram_1_re_1
  // Probe on B
  // Probe on ram_1_we_1
  // Probe on Cell_1_write_data
  // Probe on Cell_1_data
  // Probe on B
  // Probe on A_2_write_data
  // Probe on B_2_write_data
  // Probe on alu2_1_s
  // Probe on alu2_1_p
  // Probe on decoderopt_1_alu_s_p
  // Probe on decoderopt_1_alu_write_enable
  // Probe on alu2_1_write_data
  Register A_2 (
    .Clock(Clock), .Read_Enable(decoderopt_1_a_read_enable), .Read_Data(B),
    .Write_Enable(decoderopt_1_ab_write_enable), .Write_Data(A_2_write_data), .Reset(Reset), .Data(A_2_data));
  Register B_2 (
    .Clock(Clock), .Read_Enable(decoderopt_1_b_read_enable), .Read_Data(B),
    .Write_Enable(decoderopt_1_ab_write_enable), .Write_Data(B_2_write_data), .Reset(Reset), .Data(B_2_data));
  Register C (
    .Clock(Clock), .Read_Enable(decoderopt_1_c_read_enable), .Read_Data(B),
    .Write_Enable(decoderopt_1_c_write_enable), .Write_Data(C_write_data), .Reset(Reset), .Data(C_data));
  // Probe on decoderopt_1_a_read_enable
  // Probe on B
  // Probe on decoderopt_1_ab_write_enable
  // Probe on A_2_write_data
  // Probe on A_2_data
  // Probe on decoderopt_1_b_read_enable
  // Probe on B
  // Probe on decoderopt_1_ab_write_enable
  // Probe on B_2_write_data
  // Probe on B_2_data
  // Probe on decoderopt_1_c_read_enable
  // Probe on B
  // Probe on decoderopt_1_c_write_enable
  // Probe on C_write_data
  // Probe on C_data

  // Other names for the same wires on the sheet: C = Clock; R = Reset

  // Notes on the sheet:
  //   [000] Nop
  //   [001] Rom->A (Data)
  //   [010] Rom->B (Data) 
  //   [011] Rom->C (Data)
  //   [100] Add->C (S\P)
  //   [101] C->AB (A\B)
  //   [110] Ram->C (Address)
  //   [111] C->Ram (Address)
endmodule

module HS (
  input  A,
  input  B,
  output S,
  output P
);

  wire nand_1_out, nand_2_out, nand_3_out;

  nand nand_1 (nand_1_out, A, B);
  nand nand_2 (nand_2_out, A, nand_1_out);
  nand nand_3 (nand_3_out, nand_1_out, B);
  not not_1 (P, nand_1_out);
  nand nand_4 (S, nand_2_out, nand_3_out);
endmodule

// Mux
module Multiplexer_2_1 (
  input  _0,
  input  _1,
  input  Address,
  output Q
);

  wire nand_1_out, nand_2_out, not_1_out;

  not not_1 (not_1_out, Address);
  nand nand_1 (nand_1_out, _0, not_1_out);
  nand nand_2 (nand_2_out, _1, Address);
  nand nand_3 (Q, nand_1_out, nand_2_out);
endmodule

module Decoder_3_8_Invert (
  input  _0,
  input  _1,
  input  _2,
  output _0_2,
  output _1_2,
  output _2_2,
  output _3,
  output _4,
  output _5,
  output _6,
  output _7
);

  wire not_1_out, not_2_out, not_3_out;

  not not_1 (not_1_out, _0);
  not not_2 (not_2_out, _1);
  not not_3 (not_3_out, _2);
  nand nand_1 (_0_2, not_1_out, not_2_out, not_3_out);
  nand nand_2 (_1_2, _0, not_2_out, not_3_out);
  nand nand_3 (_2_2, not_1_out, not_3_out, _1);
  nand nand_4 (_3, not_3_out, _0, _1);
  nand nand_5 (_4, not_1_out, not_2_out, _2);
  nand nand_6 (_5, not_2_out, _0, _2);
  nand nand_7 (_6, not_1_out, _1, _2);
  nand nand_8 (_7, _0, _1, _2);
endmodule

module D_Trigger (
  input  C,
  input  D,
  input  R,
  output Q,
  output NQ
);

  wire nand_1_out, nand_2_out, not_1_out, not_2_out;

  not not_1 (not_1_out, D);
  not not_2 (not_2_out, R);
  nand nand_1 (nand_1_out, D, C);
  nand nand_2 (nand_2_out, C, not_1_out);
  nand nand_3 (Q, nand_1_out, NQ);
  nand nand_4 (NQ, Q, nand_2_out, not_2_out);
endmodule

module Register (
  input  Clock,
  input  Read_Enable,
  input  Read_Data,
  input  Write_Enable,
  input  Reset,
  output Data,
  output Write_Data
);

  wire d_trigger_1_nq, nand_1_out, nor_1_out, not_1_out, not_2_out;

  not not_1 (not_1_out, Clock);
  not not_2 (not_2_out, Read_Enable);
  nor nor_1 (nor_1_out, not_1_out, not_2_out);
  nand nand_1 (nand_1_out, Data, Write_Enable);
  not not_3 (Write_Data, nand_1_out);
  D_Trigger d_trigger_1 (.C(nor_1_out), .D(Read_Data), .R(Reset), .Q(Data), .NQ(d_trigger_1_nq));

  // Notes on the sheet:
  //   Входы делаем с инверторов, потому что на них нужно вешать светодиоды
endmodule

module Ram (
  input  Read_Enable,
  input  Write_Enable,
  input  Address,
  output RE_0,
  output WE_0,
  output RE_1,
  output WE_1
);

  wire not_1_out, not_2_out, not_3_out;

  not not_1 (not_1_out, Read_Enable);
  not not_2 (not_2_out, Write_Enable);
  not not_3 (not_3_out, Address);
  nor nor_1 (RE_0, Address, not_1_out);
  nor nor_2 (RE_1, not_1_out, not_3_out);
  nor nor_3 (WE_0, Address, not_2_out);
  nor nor_4 (WE_1, not_2_out, not_3_out);
endmodule

// Decoder
module DecoderOpt (
  input  _2,
  input  _1,
  input  _0,
  input  Data,
  output A_Read_Enable,
  output B_Read_Enable,
  output AB_Write_Enable,
  output C_Read_Enable,
  output C_Write_Enable,
  output Alu_Write_Enable,
  output Alu_S_P,
  output Ram_Read_Enable,
  output Ram_Write_Enable,
  output Ram_Address,
  output Bus_Data
);

  wire decoder_3_8_invert_1__1_2, decoder_3_8_invert_1__2_2, decoder_3_8_invert_1__3,
       decoder_3_8_invert_1__4, decoder_3_8_invert_1__5, decoder_3_8_invert_1__6, decoder_3_8_invert_1__7,
       nand_1_out, nand_2_out, nor_1_out, not_1_out, not_2_out, not_3_out, not_5_out, not_8_out;

  Decoder_3_8_Invert decoder_3_8_invert_1 (
    ._0(_0), ._1(_1), ._2(_2), ._1_2(decoder_3_8_invert_1__1_2), ._2_2(decoder_3_8_invert_1__2_2),
    ._3(decoder_3_8_invert_1__3), ._4(decoder_3_8_invert_1__4), ._5(decoder_3_8_invert_1__5),
    ._6(decoder_3_8_invert_1__6), ._7(decoder_3_8_invert_1__7));  // open: _0_2
  not not_1 (not_1_out, decoder_3_8_invert_1__1_2);
  not not_2 (not_2_out, decoder_3_8_invert_1__2_2);
  not not_3 (not_3_out, decoder_3_8_invert_1__3);
  not not_4 (AB_Write_Enable, decoder_3_8_invert_1__4);
  not not_5 (not_5_out, decoder_3_8_invert_1__5);
  not not_6 (Ram_Write_Enable, decoder_3_8_invert_1__6);
  not not_7 (Ram_Read_Enable, decoder_3_8_invert_1__7);
  not not_8 (not_8_out, Data);
  nand nand_1 (nand_1_out, not_8_out, not_5_out);
  nand nand_2 (nand_2_out, not_5_out, Data);
  nor nor_1 (nor_1_out, not_1_out, not_2_out, not_3_out);
  nand nand_3 (A_Read_Enable, nand_1_out, decoder_3_8_invert_1__1_2);
  nand nand_4 (B_Read_Enable, nand_2_out, decoder_3_8_invert_1__2_2);
  nand nand_5 (C_Read_Enable, decoder_3_8_invert_1__6, decoder_3_8_invert_1__4, decoder_3_8_invert_1__3);
  nand nand_6 (C_Write_Enable, decoder_3_8_invert_1__7, decoder_3_8_invert_1__5);
  nor nor_2 (Bus_Data, nor_1_out, not_8_out);

  assign Alu_S_P = Data;
  assign Alu_Write_Enable = AB_Write_Enable;
  assign Ram_Address = Data;

  // Notes on the sheet:
  //   N1     N2     N3     N4     N5     N6     N7
  //   1        2        3       4        5        6       7
  //   ND       D
  //   [000] Nop
  //   [001] Rom->A (Data)
  //   [010] Rom->B (Data) 
  //   [011] Rom->C (Data)
  //   [100] Add->C (S\P)
  //   [101] C->AB (A\B)
  //   [110] Ram->C (Address)
  //   [111] C->Ram (Address)
endmodule

// Alu
module ALU (
  input  A,
  input  B,
  input  Write_Enable,
  input  S_P,
  output S,
  output P,
  output Write_Data
);

  wire multiplexer_2_1_1_q, nand_1_out;

  not not_1 (Write_Data, nand_1_out);
  nand nand_1 (nand_1_out, multiplexer_2_1_1_q, Write_Enable);
  HS hs_1 (.A(A), .B(B), .S(S), .P(P));
  Multiplexer_2_1 multiplexer_2_1_1 (._0(S), ._1(P), .Address(S_P), .Q(multiplexer_2_1_1_q));
endmodule

module Bus (
  input  Bus_Input,
  input  Bus_Input_2,
  input  Bus_Input_3,
  input  Bus_Input_4,
  input  Bus_Input_5,
  output Bus_Output
);

  wire nor_1_out;

  nor nor_1 (nor_1_out, Bus_Input, Bus_Input_2, Bus_Input_3, Bus_Input_4, Bus_Input_5);
  not not_1 (Bus_Output, nor_1_out);
endmodule

// Alu
module ALU2 (
  input  A,
  input  B,
  input  Write_Enable,
  input  S_P,
  output S,
  output P,
  output Write_Data
);

  wire and_1_out, and_2_out, and_3_out, and_4_out, nand_1_out, nor_2_out, nor_3_out, not_1_out, not_4_out;

  nand nand_1 (nand_1_out, A, B);
  nor nor_1 (Write_Data, nor_3_out, not_1_out);
  not not_1 (not_1_out, Write_Enable);
  and and_1 (and_1_out, A, nand_1_out);
  and and_2 (and_2_out, nand_1_out, B);
  not not_2 (P, nand_1_out);
  nor nor_2 (nor_2_out, and_1_out, and_2_out);
  not not_3 (S, nor_2_out);
  not not_4 (not_4_out, S_P);
  and and_3 (and_3_out, S, not_4_out);
  and and_4 (and_4_out, S_P, P);
  nor nor_3 (nor_3_out, and_3_out, and_4_out);
endmodule
